# Fritzing sketch receptor-esp8266 (saved by Fritzing 1.0.6)
breadboards: 2

parts:
  M4 = RF 433 MHz RX (MX-05V) [part_number=MX-05V]
  S3 = Pushbutton [package="[THT]"]
  R10 = Resistor [tolerance=±5% power=0.25W resistance=10k package=THT]
  R11 = Resistor [tolerance=±5% power=0.25W resistance=220 package=THT]
  R12 = Resistor [tolerance=±5% power=0.25W resistance=10k package=THT]
  R13 = Resistor [tolerance=±5% power=0.25W resistance=10k package=THT]
  R14 = Resistor [tolerance=±5% power=0.25W resistance=220 package=THT]
  LED5 = LED - 5mm [color="Red (633nm)" current=0.030A package="5 mm [THT]"]
  U2 = LCD-16X2 [package=lcd-16x2_noholes]
  R15 = Trimmer Potentiometer [maximum_resistance=10kΩ knob_status=50% power=0.5W package=THT]
  M5 = NodeMCU ESP8266 LoLin v3 (ESP-12E)

nets:
  VCC: M4.VCC, R11.Pin_1, U2.VDD, M5.VU
  N1: M4.DATA, M4.DATA2, R10.Pin_0
  GND: M4.GND, S3.Pin_1, S3.Pin_2, R13.Pin_1, LED5.anode, U2.VSS, U2.R_W, U2.K, R15.leg1, M5.G, M5.G2, M5.G3, M5.G4, M5.G5
  N2: S3.Pin_3, S3.Pin_4, M5.D3
  N3: R10.Pin_1, R12.Pin_0, M5.D2
  N4: R11.Pin_0, U2.A
  N5: R12.Pin_1, R13.Pin_0
  N6: R14.Pin_0, M5.D8
  N7: R14.Pin_1, LED5.cathode
  N8: U2.VO, R15.wiper
  N9: U2.RS, M5.D1
  N10: U2.E, M5.D0
  N11: U2.DB4, M5.D4
  N12: U2.DB5, M5.D5
  N13: U2.DB6, M5.D6
  N14: U2.DB7, M5.D7
  N15: R15.leg2, M5.3V, M5.3V2, M5.3V3

custom parts:
  RF 433 MHz RX (MX-05V): Modulo receptor de radiofrequencia 433 MHz por modulacao de amplitude, modelo MX-05V (tambem MX-RM-5V). Placa de 30 x 14 mm, 5 V, cerca de 4 mA, sensibilidade de -105 dB. Tem quatro pinos, dois deles DATA ligados internamente: usar qualquer um. Pinagem VCC DATA DATA GND da esquerda para a direita VISTA DE CIMA; a serigrafia fica no verso, onde se le o inverso. Os receptores baratos sao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
  NodeMCU ESP8266 LoLin v3 (ESP-12E): Placa de desenvolvimento NodeMCU 1.0 com ESP8266 ESP-12E, versao LoLin v3. Placa de 59 x 31 mm, com as duas fileiras a 1,1 polegada (27,94 mm) uma da outra: ela cobre a protoboard inteira e NAO deixa coluna livre dos lados, ao contrario da Amica, que e mais estreita. Alimentacao de 4,5 a 9 V pelo VIN, ou pela micro-USB; nivel logico de 3,3 V e OS PINOS NAO SAO TOLERANTES A 5 V. Cerca de 270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
