# Fritzing sketch sketch-codigo-morse (saved by Fritzing 1.0.6)
breadboards: 2

parts:
  Componente1 = Arduino Nano (Rev3.0)
  S1 = Pushbutton [package="[THT]"]
  R1 = Resistor [tolerance=±5% power=0.25W resistance=220 package=THT]
  LED1 = LED - 5mm [color="Green (565nm)" current=0.030A package="5 mm [THT]"]
  LED2 = LED - 5mm [color="Green (565nm)" current=0.030A package="5 mm [THT]"]
  R2 = Resistor [tolerance=±5% power=0.25W resistance=220 package=THT]
  LED3 = LED - 5mm [color="Blue (470nm)" current=0.030A package="5 mm [THT]"]
  R3 = Resistor [tolerance=±5% power=0.25W resistance=220 package=THT]
  SG1 = Buzzer 12mm [package=buzzer-ccv-kit]
  Mod1 = Amica NodeMCU DEVKIT 1.0
  U1 = LCD-16X2 [package=lcd-16x2_noholes]
  LED4 = LED - 5mm [color="Red (633nm)" current=0.030A package="5 mm [THT]"]
  R4 = Resistor [tolerance=±5% power=0.25W resistance=220 package=THT]
  S2 = Pushbutton [package="[THT]"]
  R5 = Trimmer Potentiometer [maximum_resistance=10kΩ knob_status=50% power=0.5W package=THT]
  R6 = Resistor [tolerance=±5% power=0.25W resistance=10k package=THT]
  R7 = Resistor [tolerance=±5% power=0.25W resistance=10k package=THT]
  R8 = Resistor [tolerance=±5% power=0.25W resistance=10k package=THT]
  M1 = RF 433 MHz RX (MX-05V) [part_number=MX-05V]
  M2 = RF 433 MHz TX (FS1000A) [part_number=MX-FS-03V]

nets:
  GND: Componente1.GND, S1.Pin_1, S1.Pin_2, LED1.anode, LED2.anode, LED3.anode, SG1.1, M2.GND
  N1: Componente1.D2, S1.Pin_3, S1.Pin_4
  N2: Componente1.D3, R1.Pin_0
  N3: Componente1.D4, R2.Pin_0
  N4: Componente1.D5, SG1.2
  N5: Componente1.D6, R3.Pin_0
  N6: Componente1.D12/MISO, M2.DATA
  VIN: Componente1.VIN, M2.VCC
  N7: R1.Pin_1, LED1.cathode
  N8: LED2.cathode, R2.Pin_1
  N9: LED3.cathode, R3.Pin_1
  N10: Mod1.pin1, Mod1.pin_10, Mod1.pin_26, R5.leg2
  VSS: Mod1.pin2, Mod1.pin_9, Mod1.pin_25, Mod1.pin_29, U1.VSS, U1.R_W, U1.K, LED4.anode, S2.Pin_3, S2.Pin_4, R5.leg1, R6.Pin_1, M1.GND
  N11: Mod1.pin5, R4.Pin_0
  N12: Mod1.pin6, U1.DB7
  N13: Mod1.pin7, U1.DB6
  N14: Mod1.pin8, U1.DB5
  N15: Mod1.pin_11, U1.DB4
  N16: Mod1.pin_12, S2.Pin_1, S2.Pin_2
  N17: Mod1.pin_13, R7.Pin_0, R8.Pin_1
  N18: Mod1.pin_14, U1.RS
  N19: Mod1.pin_15, U1.E
  VDD: Mod1.pin_18, U1.VDD, U1.A, M1.VCC
  N20: U1.VO, R5.wiper
  N21: LED4.cathode, R4.Pin_1
  N22: R6.Pin_0, R7.Pin_1
  N23: R8.Pin_0, M1.DATA, M1.DATA2

custom parts:
  RF 433 MHz RX (MX-05V): Modulo receptor de radiofrequencia 433 MHz por modulacao de amplitude, modelo MX-05V (tambem MX-RM-5V). Placa de 30 x 14 mm, 5 V, cerca de 4 mA, sensibilidade de -105 dB. Tem quatro pinos, dois deles DATA ligados internamente: usar qualquer um. Pinagem VCC DATA DATA GND da esquerda para a direita VISTA DE CIMA; a serigrafia fica no verso, onde se le o inverso. Os receptores baratos sao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
  RF 433 MHz TX (FS1000A): Modulo transmissor de radiofrequencia 433 MHz por modulacao de amplitude (ASK/OOK), modelo MX-FS-03V, tambem serigrafado FS1000A. Placa de 19 x 19 mm, alimentacao de 3,5 a 12 V — quanto maior a tensao, maior o alcance. Um unico pino de dados. Sem antena o alcance e de centimetros: um fio reto de 17,3 cm e um quarto de onda em 433,92 MHz e resolve. Pinagem DATA VCC GND, da esquerda para a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
