# Fritzing sketch transmissor-nano (saved by Fritzing 1.0.6)
breadboards: 1

parts:
  M3 = RF 433 MHz TX (FS1000A) [part_number=MX-FS-03V]
  Componente2 = Arduino Nano (Rev3.0)
  S2 = Pushbutton [package="[THT]"]
  R4 = Resistor [tolerance=±5% power=0.25W resistance=220 package=THT]
  R5 = Resistor [tolerance=±5% power=0.25W resistance=220 package=THT]
  R6 = Resistor [tolerance=±5% power=0.25W resistance=220 package=THT]
  LED4 = LED - 5mm [color="Blue (470nm)" current=0.030A package="5 mm [THT]"]
  LED5 = LED - 5mm [color="Green (565nm)" current=0.030A package="5 mm [THT]"]
  LED6 = LED - 5mm [color="Green (565nm)" current=0.030A package="5 mm [THT]"]
  Módulo_Buzzer_GBK_P15_Ativo1 = Modulo Buzzer Ativo P15 (GBK)

nets:
  N1: M3.DATA, Componente2.D12/MISO
  VCC: M3.VCC, Componente2.5V
  GND: M3.GND, Componente2.GND, S2.Pin_1, S2.Pin_2, LED4.anode, LED5.anode, LED6.anode, Módulo_Buzzer_GBK_P15_Ativo1.GND
  N2: Componente2.D2, S2.Pin_3, S2.Pin_4
  N3: Componente2.D3, R6.Pin_0
  N4: Componente2.D4, Módulo_Buzzer_GBK_P15_Ativo1.SINAL
  N5: Componente2.D5, R5.Pin_0
  N6: Componente2.D6, R4.Pin_0
  N7: R4.Pin_1, LED4.cathode
  N8: R5.Pin_1, LED5.cathode
  N9: R6.Pin_1, LED6.cathode

custom parts:
  RF 433 MHz TX (FS1000A): Modulo transmissor de radiofrequencia 433 MHz por modulacao de amplitude (ASK/OOK), modelo MX-FS-03V, tambem serigrafado FS1000A. Placa de 19 x 19 mm, alimentacao de 3,5 a 12 V — quanto maior a tensao, maior o alcance. Um unico pino de dados. Sem antena o alcance e de centimetros: um fio reto de 17,3 cm e um quarto de onda em 433,92 MHz e resolve. Pinagem DATA VCC GND, da esquerda para a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
  Modulo Buzzer Ativo P15 (GBK): Modulo buzzer ativo GBK P15, placa de 32 x 15 x 11 mm. Ativo quer dizer que o oscilador esta dentro: toca uma nota so, e o codigo apenas liga e desliga. Para tocar melodia seria preciso um passivo. Alimentacao de 3,3 a 5 V, ate 42 mA, saida acima de 85 dB. Dois pinos numa das pontas, GND em cima e SINAL embaixo com a serigrafia legivel. A POLARIDADE DE ACIONAMENTO NAO FOI VERIFICADA: varios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
